// Logisim project x.circ as structural Verilog: 2 circuits, main circuit main
module main (
  input  in_1,
  input  in_2,
  output out_3
);

  x x_1 (.in_1(in_1), .in_2(in_2), .out_3(out_3));
endmodule

module x (
  input  in_1,
  input  in_2,
  output out_3
);

  and and_1 (out_3, in_1, in_2);
endmodule
